// Logisim project processor.circ as structural Verilog
module main (
  input  [2:0] in_1
);

  wire clk, res;
  wire [1:0] keyboard_3_dir;
  wire [4:0] control_1_lb, control_1_rb, control_1_x, control_1_y, lstep_1_out_4, n8rows_1_out_14,
       n8rows_1_out_15, n8rows_1_out_16, n8rows_1_out_17, n8rows_1_out_18, n8rows_2_out_14, n8rows_2_out_15,
       n8rows_2_out_16, n8rows_2_out_17, n8rows_2_out_18, n8rows_3_out_14, n8rows_3_out_15, n8rows_3_out_16,
       n8rows_3_out_17, n8rows_3_out_18, register_1_q;
  wire [6:0] keyboard_1_data, keyboard_2_data;
  wire [7:0] Lscore, Rscore;
  wire [31:0] color_1_out_4, n8rows_1_out_6, n8rows_1_out_7, n8rows_1_out_8, n8rows_1_out_9, n8rows_1_out_10,
       n8rows_1_out_11, n8rows_1_out_12, n8rows_1_out_13, n8rows_2_out_6, n8rows_2_out_7, n8rows_2_out_8,
       n8rows_2_out_9, n8rows_2_out_10, n8rows_2_out_11, n8rows_2_out_12, n8rows_2_out_13, n8rows_3_out_6,
       n8rows_3_out_7, n8rows_3_out_8, n8rows_3_out_9, n8rows_3_out_10, n8rows_3_out_11, n8rows_3_out_12,
       n8rows_3_out_13, n8rows_4_out_6, n8rows_4_out_7, n8rows_4_out_8, n8rows_4_out_9, n8rows_4_out_10,
       n8rows_4_out_11, n8rows_4_out_12, n8rows_4_out_13;

  Clock clock_1 (.out(clk));
  Button button_1 (.out(res));
  Keyboard keyboard_1 (.clk(clk), .data(keyboard_1_data));  // open: re, clr, avail
  Keyboard keyboard_2 (.clk(clk), .data(keyboard_2_data));  // open: re, clr, avail
  control control_1 (
    .res(res), .kin(keyboard_1_data), .x(control_1_x), .lb(control_1_lb), .clk(clk), .y(control_1_y),
    .rb(control_1_rb), .enemyscore(Rscore), .myscore(Lscore));  // open: ctr, tst
  keyboard keyboard_3 (.keyb(keyboard_2_data), .dir(keyboard_3_dir));
  Hex_Digit_Display hex_digit_display_1 (.value(Lscore[3:0]));  // open: dp
  Hex_Digit_Display hex_digit_display_2 (.value(Lscore[7:4]));  // open: dp
  lstep lstep_1 (.clk(clk), .move(keyboard_3_dir), .rs(res), .out_4(lstep_1_out_4));
  _8rows u_8rows_1 (
    .in_1({5{1'b0}}), .in_2(control_1_x), .in_3(control_1_y), .in_4(control_1_lb), .in_5(control_1_rb),
    .out_6(n8rows_1_out_6), .out_7(n8rows_1_out_7), .out_8(n8rows_1_out_8), .out_9(n8rows_1_out_9),
    .out_10(n8rows_1_out_10), .out_11(n8rows_1_out_11), .out_12(n8rows_1_out_12), .out_13(n8rows_1_out_13),
    .out_14(n8rows_1_out_14), .out_15(n8rows_1_out_15), .out_16(n8rows_1_out_16), .out_17(n8rows_1_out_17),
    .out_18(n8rows_1_out_18));
  DotMatrix #(.matrixcols(32), .matrixrows(32)) dotmatrix_1 (
    .col0(n8rows_1_out_6), .col1(n8rows_1_out_7), .col2(n8rows_1_out_8), .col3(n8rows_1_out_9),
    .col4(n8rows_1_out_10), .col5(n8rows_1_out_11), .col6(n8rows_1_out_12), .col7(n8rows_1_out_13),
    .col8(n8rows_2_out_6), .col9(n8rows_2_out_7), .col10(n8rows_2_out_8), .col11(n8rows_2_out_9),
    .col12(n8rows_2_out_10), .col13(n8rows_2_out_11), .col14(n8rows_2_out_12), .col15(n8rows_2_out_13),
    .col16(n8rows_3_out_6), .col17(n8rows_3_out_7), .col18(n8rows_3_out_8), .col19(n8rows_3_out_9),
    .col20(n8rows_3_out_10), .col21(n8rows_3_out_11), .col22(n8rows_3_out_12), .col23(n8rows_3_out_13),
    .col24(n8rows_4_out_6), .col25(n8rows_4_out_7), .col26(n8rows_4_out_8), .col27(n8rows_4_out_9),
    .col28(n8rows_4_out_10), .col29(n8rows_4_out_11), .col30(n8rows_4_out_12), .col31(n8rows_4_out_13));
  DotMatrix #(.matrixcols(1), .matrixrows(32)) dotmatrix_2 (.col0(color_1_out_4));
  Register #(.width(5)) register_1 (.D(lstep_1_out_4), .Q(register_1_q), .clk(clk));  // open: en, clr
  _8rows u_8rows_2 (
    .in_1(n8rows_1_out_14), .in_2(n8rows_1_out_15), .in_3(n8rows_1_out_16), .in_4(n8rows_1_out_17),
    .in_5(n8rows_1_out_18), .out_6(n8rows_2_out_6), .out_7(n8rows_2_out_7), .out_8(n8rows_2_out_8),
    .out_9(n8rows_2_out_9), .out_10(n8rows_2_out_10), .out_11(n8rows_2_out_11), .out_12(n8rows_2_out_12),
    .out_13(n8rows_2_out_13), .out_14(n8rows_2_out_14), .out_15(n8rows_2_out_15), .out_16(n8rows_2_out_16),
    .out_17(n8rows_2_out_17), .out_18(n8rows_2_out_18));
  _8rows u_8rows_3 (
    .in_1(n8rows_2_out_14), .in_2(n8rows_2_out_15), .in_3(n8rows_2_out_16), .in_4(n8rows_2_out_17),
    .in_5(n8rows_2_out_18), .out_6(n8rows_3_out_6), .out_7(n8rows_3_out_7), .out_8(n8rows_3_out_8),
    .out_9(n8rows_3_out_9), .out_10(n8rows_3_out_10), .out_11(n8rows_3_out_11), .out_12(n8rows_3_out_12),
    .out_13(n8rows_3_out_13), .out_14(n8rows_3_out_14), .out_15(n8rows_3_out_15), .out_16(n8rows_3_out_16),
    .out_17(n8rows_3_out_17), .out_18(n8rows_3_out_18));
  _8rows u_8rows_4 (
    .in_1(n8rows_3_out_14), .in_2(n8rows_3_out_15), .in_3(n8rows_3_out_16), .in_4(n8rows_3_out_17),
    .in_5(n8rows_3_out_18), .out_6(n8rows_4_out_6), .out_7(n8rows_4_out_7), .out_8(n8rows_4_out_8),
    .out_9(n8rows_4_out_9), .out_10(n8rows_4_out_10), .out_11(n8rows_4_out_11), .out_12(n8rows_4_out_12),
    .out_13(n8rows_4_out_13));  // open: out_14, out_15, out_16, out_17, out_18
  Hex_Digit_Display hex_digit_display_3 (.value(Rscore[7:4]));  // open: dp
  Hex_Digit_Display hex_digit_display_4 (.value(Rscore[3:0]));  // open: dp
  DotMatrix #(.matrixcols(1), .matrixrows(32)) dotmatrix_3 (.col0(color_1_out_4));
  color color_1 (.xball(control_1_y), .mode(in_1), .clk(clk), .out_4(color_1_out_4));

  // Notes on the sheet:
  //   000 - y ball
  //   001 - gravity
  //   010 reverse grav
  //   011 - fire
endmodule

module control (
  input  [6:0] kin,
  input  [1:0] ctr,
  input  res,
  input  clk,
  input  [4:0] tst,
  output [4:0] x,
  output [4:0] lb,
  output [4:0] rb,
  output [7:0] myscore,
  output [4:0] y,
  output [7:0] enemyscore
);

  wire _2clk, _4clk, _8clk, clllision_1_out_5, clllision_2_out_5, comparator_1_eq, comparator_2_eq,
       comparator_5_eq, comparator_6_eq, d_ff_1_q, d_ff_2_q, d_ff_3_q, goal1, goal2, not_1_out, not_2_out,
       not_4_out, not_6_out, or_1_out, or_2_out, or_3_out, register_1_q, register_2_q, vx, vy, xor_1_out;
  wire [1:0] keyboard_1_dir;
  wire [4:0] adder_3_out, adder_4_out, controlled_buffer_1_out, controlled_buffer_3_out, multiplexer_1_out,
       multiplexer_2_out, rb_q;
  wire [7:0] adder_1_out, adder_2_out;

  Adder adder_1 (.a(8'h6), .b(myscore), .out(adder_1_out));  // open: cin, cout
  Adder adder_2 (.a(8'h6), .b(enemyscore), .out(adder_2_out));  // open: cin, cout
  Register #(.width(1)) state ();  // open: D, en, Q, clk, clr
  Counter counter_1 (
    .load(comparator_1_eq), .D(adder_1_out), .count(goal1), .Q(myscore), .clk(_2clk), .clr(res));  // open: carry
  Counter counter_2 (
    .load(comparator_2_eq), .D(adder_2_out), .count(goal2), .Q(enemyscore), .clk(_2clk), .clr(res));  // open: carry
  keyboard keyboard_1 (.keyb(kin), .dir(keyboard_1_dir));
  lstep lstep_1 ();  // open: clk, move, rs, out_4
  rstep rstep_1 (.in_1(kin), .clk(clk), .rs(res), .out_4(rb));
  Comparator #(.width(4)) comparator_1 (.a(myscore[3:0]), .b(4'b1010), .eq(comparator_1_eq));  // open: gt, lt
  Comparator #(.width(4)) comparator_2 (.a(enemyscore[3:0]), .b(4'b1010), .eq(comparator_2_eq));  // open: gt, lt
  lstep lstep_2 (.clk(clk), .move(keyboard_1_dir), .rs(res), .out_4(lb));
  Register #(.width(5)) u_rb (.Q(rb_q));  // open: D, en, clk, clr
  not not_1 (not_1_out, res);
  not not_2 (not_2_out, res);
  xor xor_1 (xor_1_out, vx, or_1_out);
  D_Flip_Flop d_ff_1 (.clk(clk), .D(_2clk), .Q(d_ff_1_q));  // open: Qn, preset, en, reset
  Adder #(.width(5)) adder_3 (.a(x), .b(multiplexer_1_out), .out(adder_3_out));  // open: cin, cout
  Multiplexer #(.width(5), .enable("false")) multiplexer_1 (
    .in0({5{1'b1}}), .in1(5'b00001), .out(multiplexer_1_out), .sel(xor_1_out));
  D_Flip_Flop d_ff_2 (.clk(_2clk), .D(_4clk), .Q(d_ff_2_q));  // open: Qn, preset, en, reset
  not not_3 (_2clk, d_ff_1_q);
  Multiplexer #(.width(5), .enable("false")) multiplexer_2 (
    .in0({5{1'b1}}), .in1(5'b00001), .out(multiplexer_2_out), .sel(vy));
  assign controlled_buffer_1_out = not_1_out ? adder_3_out : 5'bz;  // Controlled_Buffer controlled_buffer_1
  not not_4 (not_4_out, not_1_out);
  assign controlled_buffer_1_out = not_4_out ? 5'b00011 : 5'bz;  // Controlled_Buffer controlled_buffer_2
  D_Flip_Flop d_ff_3 (.clk(_4clk), .D(_8clk), .Q(d_ff_3_q));  // open: Qn, preset, en, reset
  not not_5 (_4clk, d_ff_2_q);
  Adder #(.width(5)) adder_4 (.a(y), .b(multiplexer_2_out), .out(adder_4_out));  // open: cin, cout
  assign controlled_buffer_3_out = not_2_out ? adder_4_out : 5'bz;  // Controlled_Buffer controlled_buffer_3
  not not_6 (not_6_out, not_2_out);
  assign controlled_buffer_3_out = not_6_out ? 5'b01111 : 5'bz;  // Controlled_Buffer controlled_buffer_4
  Register #(.width(1)) register_1 (.D(not_1_out), .Q(register_1_q), .clk(_2clk));  // open: en, clr
  not not_7 (_8clk, d_ff_3_q);
  clllision clllision_1 (.bat(lb), .yball(y), .out_5(clllision_1_out_5), .xball(x), .in(5'b00010));
  clllision clllision_2 (.bat(rb), .yball(y), .out_5(clllision_2_out_5), .xball(x), .in(5'b11101));
  Register #(.width(1)) register_2 (.D(not_2_out), .Q(register_2_q), .clk(_4clk));  // open: en, clr
  Register #(.width(5)) u_x (.D(controlled_buffer_1_out), .en(register_1_q), .Q(x), .clk(_2clk));  // open: clr
  Register #(.width(5)) u_y (.D(controlled_buffer_3_out), .en(register_2_q), .Q(y), .clk(_4clk));  // open: clr
  Comparator #(.width(5)) comparator_3 (.a(x), .b({5{1'b0}}), .eq(goal2));  // open: gt, lt
  Comparator #(.width(5)) comparator_4 (.a(x), .b({5{1'b1}}), .eq(goal1));  // open: gt, lt
  Comparator #(.width(5)) comparator_5 (.a(y), .b({5{1'b0}}), .eq(comparator_5_eq));  // open: gt, lt
  Comparator #(.width(5)) comparator_6 (.a(y), .b({5{1'b1}}), .eq(comparator_6_eq));  // open: gt, lt
  or or_1 (or_1_out, goal2, clllision_1_out_5, goal1, clllision_2_out_5);
  or or_2 (or_2_out, comparator_5_eq, comparator_6_eq);
  or or_3 (or_3_out, goal2, clllision_1_out_5);
  Register #(.width(1)) u_vx (.D(or_3_out), .en(or_1_out), .Q(vx), .clk(_2clk));  // open: clr
  Register #(.width(1)) u_vy (.D(comparator_5_eq), .en(or_2_out), .Q(vy), .clk(_2clk));  // open: clr

  // Other names for the same wires on the sheet: state = res

  // Notes on the sheet:
  //   Collision
  //   x culc
  //   y culc
  //   x =1 - up
  //   x =0 - down
  //   y =1 - right
  //   y =0 - left
endmodule

module lstep (
  input  clk,
  input  [1:0] move,
  input  rs,
  output [4:0] out_4
);

  wire _2clk, clock_1_out, comparator_1_gt, d_ff_1_q, not_2_out;
  wire [4:0] adder_1_out, controlled_buffer_1_out, multiplexer_1_out;

  D_Flip_Flop d_ff_1 (.clk(clk), .D(_2clk), .Q(d_ff_1_q));  // open: Qn, preset, en, reset
  not not_1 (_2clk, d_ff_1_q);
  Clock clock_1 (.out(clock_1_out));
  Multiplexer #(.select(2), .width(5), .enable("false")) multiplexer_1 (
    .in0({5{1'b0}}), .in1(5'b00001), .in2({5{1'b1}}), .out(multiplexer_1_out), .sel(move));  // open: in3
  // Probe on controlled_buffer_1_out
  Adder #(.width(5)) adder_1 (.a(multiplexer_1_out), .b(out_4), .out(adder_1_out));  // open: cin, cout
  assign controlled_buffer_1_out = not_2_out ? adder_1_out : 5'bz;  // Controlled_Buffer controlled_buffer_1
  not not_2 (not_2_out, rs);
  assign controlled_buffer_1_out = rs ? 5'b01110 : 5'bz;  // Controlled_Buffer controlled_buffer_2
  Comparator #(.width(5), .mode("unsigned")) comparator_1 (
    .a(5'b11110), .b(controlled_buffer_1_out), .gt(comparator_1_gt));  // open: eq, lt
  // Probe on out_4
  Register #(.width(5)) register_1 (
    .D(controlled_buffer_1_out), .en(comparator_1_gt), .Q(out_4), .clk(clk));  // open: clr
endmodule

module m (
);

  DotMatrix #(.matrixcols(32), .matrixrows(20)) dotmatrix_1 ();  // open: col0, col1, col2, col3, col4, col5, col6, col7, col8, col9, col10, col11, col12, col13, col14, col15, col16, col17, col18, col19, col20, col21, col22, col23, col24, col25, col26, col27, col28, col29, col30, col31
endmodule

module gir (
);

  wire and_2_out, and_3_out, cdm_8_mark5_1_p4, cdm_8_mark5_1_p5, cdm_8_mark5_1_p7, cdm_8_mark5_1_p8,
       cdm_8_mark5_1_p9, cdm_8_mark5_1_p10, cdm_8_mark5_1_p11, cdm_8_mark5_1_p12, cdm_8_mark5_1_p13, clk,
       decoder_1_out0, decoder_1_out1, decoder_2_out0, decoder_2_out1, decoder_2_out2, decoder_2_out3,
       decoder_2_out4, decoder_2_out5, decoder_2_out6, decoder_2_out7, decoder_2_out8, decoder_2_out9,
       decoder_2_out10, decoder_2_out11, decoder_2_out12, decoder_2_out13, decoder_2_out14, decoder_2_out15,
       IAck, IOsel, IRQ, not_1_out, not_2_out, READwrite;
  wire [2:0] vec;
  wire [3:0] IOaddr;
  wire [6:0] keyboard_1_data;
  wire [7:0] cdm_8_mark5_1_p16, cdm_8_mark5_1_p17, IOdat, register_2_q;
  wire [7:4] cdm_8_mark5_1_p15;

  Demultiplexer demultiplexer_1 ();  // open: out0, out1, in, sel, en
  Clock clock_1 (.out(clk));
  // Probe on cdm_8_mark5_1_p5
  // Probe on cdm_8_mark5_1_p4
  // Probe on cdm_8_mark5_1_p8
  // Probe on cdm_8_mark5_1_p7
  // Probe on cdm_8_mark5_1_p10
  // Probe on cdm_8_mark5_1_p9
  and and_1 (IOsel, cdm_8_mark5_1_p15[4], cdm_8_mark5_1_p15[5], cdm_8_mark5_1_p15[6], cdm_8_mark5_1_p15[7], decoder_1_out1);
  // Probe on cdm_8_mark5_1_p11
  Decoder #(.disabled(0)) decoder_1 (
    .out0(decoder_1_out0), .out1(decoder_1_out1), .sel(cdm_8_mark5_1_p12), .en(cdm_8_mark5_1_p13));
  // CdM_8_mark5 cdm_8_mark5_1: pin names not known; wires that end beside it: IRQ, vec, IAck, cdm_8_mark5_1_p4, cdm_8_mark5_1_p5, clk, cdm_8_mark5_1_p7, cdm_8_mark5_1_p8, cdm_8_mark5_1_p9, cdm_8_mark5_1_p10, cdm_8_mark5_1_p11, cdm_8_mark5_1_p12, cdm_8_mark5_1_p13, READwrite, {cdm_8_mark5_1_p15, IOaddr}, cdm_8_mark5_1_p16, cdm_8_mark5_1_p17
  not not_1 (not_1_out, READwrite);
  assign IOdat = not_1_out ? cdm_8_mark5_1_p16 : 8'bz;  // Controlled_Buffer controlled_buffer_1
  assign cdm_8_mark5_1_p17 = READwrite ? IOdat : 8'bz;  // Controlled_Buffer controlled_buffer_2
  and and_2 (and_2_out, decoder_1_out1, ~IOsel);  // AND_Gate
  // Probe on {cdm_8_mark5_1_p15, IOaddr}
  not not_2 (not_2_out, clk);
  Keyboard keyboard_1 (.clk(clk), .data(keyboard_1_data));  // open: re, clr, avail
  // Probe on IOdat
  RAM ram_1 (
    .addr({cdm_8_mark5_1_p15, IOaddr}), .data(IOdat), .sel(and_2_out), .clk(not_2_out), .ld(READwrite));  // open: clr
  ROM rom_1 (.addr({cdm_8_mark5_1_p15, IOaddr}), .data(IOdat), .sel(decoder_1_out0));
  Register #(.width(7)) register_1 (.D(keyboard_1_data), .clk(clk));  // open: en, Q, clr
  and and_3 (and_3_out, IOsel, IOaddr[0], ~IOaddr[1], ~IOaddr[2], ~IOaddr[3]);  // AND_Gate
  Decoder #(.select(4), .enable("false")) decoder_2 (
    .out0(decoder_2_out0), .out1(decoder_2_out1), .out2(decoder_2_out2), .out3(decoder_2_out3),
    .out4(decoder_2_out4), .out5(decoder_2_out5), .out6(decoder_2_out6), .out7(decoder_2_out7),
    .out8(decoder_2_out8), .out9(decoder_2_out9), .out10(decoder_2_out10), .out11(decoder_2_out11),
    .out12(decoder_2_out12), .out13(decoder_2_out13), .out14(decoder_2_out14), .out15(decoder_2_out15),
    .sel(register_2_q[3:0]));
  Register register_2 (.D(IOdat), .en(and_3_out), .Q(register_2_q), .clk(clk));  // open: clr
  DotMatrix #(.inputtype("row"), .matrixcols(1), .matrixrows(1)) dotmatrix_1 (.row0(decoder_2_out0));
  DotMatrix #(.inputtype("row"), .matrixcols(1), .matrixrows(1)) dotmatrix_2 (.row0(decoder_2_out1));
  DotMatrix #(.inputtype("row"), .matrixcols(1), .matrixrows(1)) dotmatrix_3 (.row0(decoder_2_out2));
  DotMatrix #(.inputtype("row"), .matrixcols(1), .matrixrows(1)) dotmatrix_4 (.row0(decoder_2_out3));
  DotMatrix #(.inputtype("row"), .matrixcols(1), .matrixrows(1)) dotmatrix_5 (.row0(decoder_2_out4));
  DotMatrix #(.inputtype("row"), .matrixcols(1), .matrixrows(1)) dotmatrix_6 (.row0(decoder_2_out5));
  DotMatrix #(.inputtype("row"), .matrixcols(1), .matrixrows(1)) dotmatrix_7 (.row0(decoder_2_out6));
  DotMatrix #(.inputtype("row"), .matrixcols(1), .matrixrows(1)) dotmatrix_8 (.row0(decoder_2_out7));
  DotMatrix #(.inputtype("row"), .matrixcols(1), .matrixrows(1)) dotmatrix_9 (.row0(decoder_2_out8));
  DotMatrix #(.inputtype("row"), .matrixcols(1), .matrixrows(1)) dotmatrix_10 (.row0(decoder_2_out9));
  DotMatrix #(.inputtype("row"), .matrixcols(1), .matrixrows(1)) dotmatrix_11 (.row0(decoder_2_out10));
  DotMatrix #(.inputtype("row"), .matrixcols(1), .matrixrows(1)) dotmatrix_12 (.row0(decoder_2_out11));
  DotMatrix #(.inputtype("row"), .matrixcols(1), .matrixrows(1)) dotmatrix_13 (.row0(decoder_2_out12));
  DotMatrix #(.inputtype("row"), .matrixcols(1), .matrixrows(1)) dotmatrix_14 (.row0(decoder_2_out13));
  DotMatrix #(.inputtype("row"), .matrixcols(1), .matrixrows(1)) dotmatrix_15 (.row0(decoder_2_out14));
  DotMatrix #(.inputtype("row"), .matrixcols(1), .matrixrows(1)) dotmatrix_16 (.row0(decoder_2_out15));

  // Notes on the sheet:
  //   contents of rom_1 (hex, n*v repeats v):
  //   cd f0 d1 f d3 f1 76 ec d d2 0 ee e 8e ae ee 6 d4
endmodule

module xball (
  input  clk,
  input  state,
  input  vx,
  output [4:0] out_4
);

  wire not_1_out, not_2_out;
  wire [4:0] adder_1_out, multiplexer_1_out, register_1_q;

  not not_1 (not_1_out, state);
  Adder #(.width(5)) adder_1 (.a(register_1_q), .b(multiplexer_1_out), .out(adder_1_out));  // open: cin, cout
  Multiplexer #(.width(5), .enable("false")) multiplexer_1 (
    .in0(5'b11110), .in1(5'b00010), .out(multiplexer_1_out), .sel(vx));
  Register #(.width(5)) register_1 (.D(adder_1_out), .en(not_1_out), .Q(register_1_q), .clk(clk));  // open: clr
  assign out_4 = not_1_out ? register_1_q : 5'bz;  // Controlled_Buffer controlled_buffer_1
  not not_2 (not_2_out, not_1_out);
  assign out_4 = not_2_out ? 5'b01001 : 5'bz;  // Controlled_Buffer controlled_buffer_2
endmodule

module clllision (
  input  [4:0] bat,
  input  [4:0] yball,
  input  [4:0] in,
  input  [4:0] xball,
  output out_5
);

  wire comparator_1_eq, comparator_2_eq, comparator_3_eq, comparator_4_eq, or_1_out;
  wire [4:0] adder_1_out, adder_2_out;

  Adder #(.width(5)) adder_1 (.a(5'b00001), .b(bat), .out(adder_1_out));  // open: cin, cout
  Adder #(.width(5)) adder_2 (.a(bat), .b(5'b00010), .out(adder_2_out));  // open: cin, cout
  Comparator #(.width(5)) comparator_1 (.a(adder_1_out), .b(yball), .eq(comparator_1_eq));  // open: gt, lt
  Comparator #(.width(5)) comparator_2 (.a(bat), .b(yball), .eq(comparator_2_eq));  // open: gt, lt
  Comparator #(.width(5)) comparator_3 (.a(adder_2_out), .b(yball), .eq(comparator_3_eq));  // open: gt, lt
  Comparator #(.width(5)) comparator_4 (.a(in), .b(xball), .eq(comparator_4_eq));  // open: gt, lt
  or or_1 (or_1_out, comparator_1_eq, comparator_2_eq, comparator_3_eq);
  and and_1 (out_5, or_1_out, comparator_4_eq);
endmodule

module rstep (
  input  [6:0] in_1,
  input  clk,
  input  rs,
  output [4:0] out_4
);

  wire clock_1_out, comparator_3_gt, not_1_out;
  wire [1:0] comparator_1_eq;
  wire [4:0] adder_1_out, controlled_buffer_1_out, multiplexer_1_out;

  Comparator #(.width(7)) comparator_1 (.a(in_1), .b(7'b0111000), .eq(comparator_1_eq[0]));  // open: gt, lt
  Comparator #(.width(7)) comparator_2 (.a(in_1), .b(7'b0110010), .eq(comparator_1_eq[1]));  // open: gt, lt
  Clock clock_1 (.out(clock_1_out));
  Multiplexer #(.select(2), .width(5), .enable("false")) multiplexer_1 (
    .in0({5{1'b0}}), .in1(5'b00001), .in2({5{1'b1}}), .out(multiplexer_1_out), .sel(comparator_1_eq));  // open: in3
  // Probe on controlled_buffer_1_out
  assign controlled_buffer_1_out = not_1_out ? adder_1_out : 5'bz;  // Controlled_Buffer controlled_buffer_1
  Adder #(.width(5)) adder_1 (.a(multiplexer_1_out), .b(out_4), .out(adder_1_out));  // open: cin, cout
  not not_1 (not_1_out, rs);
  Comparator #(.width(5), .mode("unsigned")) comparator_3 (
    .a(5'b11110), .b(controlled_buffer_1_out), .gt(comparator_3_gt));  // open: eq, lt
  Register #(.width(5)) register_1 (
    .D(controlled_buffer_1_out), .en(comparator_3_gt), .Q(out_4), .clk(clk));  // open: clr
  assign controlled_buffer_1_out = rs ? 5'b01110 : 5'bz;  // Controlled_Buffer controlled_buffer_2
  // Probe on out_4

  // Notes on the sheet:
  //   ascii 8
  //   ascii 2
  //   UP
  //   DOWN
endmodule

module color (
  input  [4:0] xball,
  input  [2:0] mode,
  input  clk,
  output [31:0] out_4
);

  wire _4clk, _8clk, and_1_out, and_2_out, and_3_out, and_4_out, comparator_1_eq, d_ff_1_q, d_ff_2_q,
       d_ff_3_q, not_2_out, undriven;
  wire [1:0] adder_1_out, register_1_q;
  wire [2:0] adder_2_out, register_2_q;
  wire [3:0] decoder_2_out3;
  wire [4:2] decoder_3_out2;
  wire [31:0] decoder_1_out0;
  wire [31:25] or_1_out;

  not not_1 (_4clk, d_ff_1_q);
  D_Flip_Flop d_ff_1 (.clk(clk), .D(_4clk), .Q(d_ff_1_q));  // open: Qn, preset, en, reset
  D_Flip_Flop d_ff_2 (.clk(_4clk), .D(not_2_out), .Q(d_ff_2_q));  // open: Qn, preset, en, reset
  not not_2 (not_2_out, d_ff_2_q);
  D_Flip_Flop d_ff_3 (.clk(not_2_out), .D(_8clk), .Q(d_ff_3_q));  // open: Qn, preset, en, reset
  Decoder #(.select(5)) decoder_1 (
    .out0(decoder_1_out0[0]), .out1(decoder_1_out0[1]), .out2(decoder_1_out0[2]), .out3(decoder_1_out0[3]),
    .out4(decoder_1_out0[4]), .out5(decoder_1_out0[5]), .out6(decoder_1_out0[6]), .out7(decoder_1_out0[7]),
    .out8(decoder_1_out0[8]), .out9(decoder_1_out0[9]), .out10(decoder_1_out0[10]),
    .out11(decoder_1_out0[11]), .out12(decoder_1_out0[12]), .out13(decoder_1_out0[13]),
    .out14(decoder_1_out0[14]), .out15(decoder_1_out0[15]), .out16(decoder_1_out0[16]),
    .out17(decoder_1_out0[17]), .out18(decoder_1_out0[18]), .out19(decoder_1_out0[19]),
    .out20(decoder_1_out0[20]), .out21(decoder_1_out0[21]), .out22(decoder_1_out0[22]),
    .out23(decoder_1_out0[23]), .out24(decoder_1_out0[24]), .out25(decoder_1_out0[25]),
    .out26(decoder_1_out0[26]), .out27(decoder_1_out0[27]), .out28(decoder_1_out0[28]),
    .out29(decoder_1_out0[29]), .out30(decoder_1_out0[30]), .out31(decoder_1_out0[31]), .sel(xball),
    .en(and_1_out));
  and and_1 (and_1_out, ~mode[2], ~mode[1], ~mode[0]);  // AND_Gate
  not not_3 (_8clk, d_ff_3_q);
  assign out_4 = and_1_out ? decoder_1_out0 : 32'bz;  // Controlled_Buffer controlled_buffer_1
  and and_2 (and_2_out, mode[0], ~mode[1], ~mode[2]);  // AND_Gate
  Adder #(.width(2)) adder_1 (.a(register_1_q), .b(2'b01), .out(adder_1_out));  // open: cin, cout
  and and_3 (and_3_out, ~mode[0], mode[1], ~mode[2]);  // AND_Gate
  Register #(.width(2)) register_1 (.D(adder_1_out), .Q(register_1_q), .clk(_8clk), .clr(undriven));  // open: en
  Decoder #(.select(2), .enable("false")) decoder_2 (
    .out0(decoder_2_out3[0]), .out1(decoder_2_out3[1]), .out2(decoder_2_out3[2]), .out3(decoder_2_out3[3]),
    .sel(register_1_q));
  assign out_4 = and_2_out ? {decoder_2_out3, decoder_2_out3, decoder_2_out3, decoder_2_out3, decoder_2_out3[0], decoder_2_out3[1], decoder_2_out3[2], decoder_2_out3[3], decoder_2_out3[0], decoder_2_out3[1], decoder_2_out3[2], decoder_2_out3[3], decoder_2_out3[0], decoder_2_out3[1], decoder_2_out3[2], decoder_2_out3[3], decoder_2_out3[0], decoder_2_out3[1], decoder_2_out3[2], decoder_2_out3[3]} : 32'bz;  // Controlled_Buffer controlled_buffer_2
  assign out_4 = and_3_out ? {decoder_2_out3[0], decoder_2_out3[1], decoder_2_out3[2], decoder_2_out3[3], decoder_2_out3[0], decoder_2_out3[1], decoder_2_out3[2], decoder_2_out3[3], decoder_2_out3[0], decoder_2_out3[1], decoder_2_out3[2], decoder_2_out3[3], decoder_2_out3[0], decoder_2_out3[1], decoder_2_out3[2], {2{decoder_2_out3[3]}}, decoder_2_out3[2:0], decoder_2_out3, decoder_2_out3, decoder_2_out3} : 32'bz;  // Controlled_Buffer controlled_buffer_3
  and and_4 (and_4_out, mode[0], mode[1], ~mode[2]);  // AND_Gate
  assign out_4 = and_4_out ? {or_1_out, or_1_out[29:25], or_1_out[29:25], or_1_out[29:25], or_1_out[29:25], or_1_out[29:25]} : 32'bz;  // Controlled_Buffer controlled_buffer_4
  Adder #(.width(3)) adder_2 (.a(register_2_q), .b(3'b001), .out(adder_2_out));  // open: cin, cout
  Comparator #(.width(3)) comparator_1 (.a(3'b101), .b(register_2_q), .eq(comparator_1_eq));  // open: gt, lt
  Register #(.width(3)) register_2 (.D(adder_2_out), .Q(register_2_q), .clk(_4clk), .clr(comparator_1_eq));  // open: en
  Decoder #(.select(3), .enable("false")) decoder_3 (
    .out0(or_1_out[30]), .out1(or_1_out[31]), .out2(decoder_3_out2[2]), .out3(decoder_3_out2[3]),
    .out4(decoder_3_out2[4]), .sel(register_2_q));  // open: out5, out6, out7
  assign or_1_out[29:25] = {decoder_3_out2, or_1_out[31:30]} | {or_1_out[30], decoder_3_out2, or_1_out[31]};  // OR_Gate or_1, 5 bits wide
endmodule
